# Fritzing sketch navigation (saved by Fritzing 0.9.2b)
breadboards: 1

parts:
  U1 = atmega328 [package=dip]
  XTAL1 = Crystal [frequency="16 Mhz" package=THT]
  IC1 = IC, DIP package, 20 pins [chip_label=74LVC244]
  GPS1 = female pin header, 9 pins [form="♀ (female)"]
  Raspberry_Pi_2 = Raspberry Pi 2
  Power = shrouded pin header, 6 pins [form="♂ (shrouded male)"]
  C1 = Ceramic Capacitor [capacitance=22pF package="100 mil [THT, multilayer]"]
  C2 = Ceramic Capacitor [capacitance=22pF package="100 mil [THT, multilayer]"]
  C3 = Ceramic Capacitor [capacitance=100nF package="100 mil [THT, multilayer]"]
  C4 = Ceramic Capacitor [capacitance=100nF package="100 mil [THT, multilayer]"]
  R1 = Resistor [tolerance=±5% resistance=10k package=THT]
  Q1 = MOSFET-NCHANNEL [package=to-92]
  R2 = Resistor [tolerance=±5% resistance=10k package=THT]
  R3 = Resistor [tolerance=±5% resistance=100k package=THT]

nets:
  N1: U1.RESET, Q1.D, R2.Pin_1
  N2: U1.VCC, U1.AVCC, Power.pin1, C3.0, C4.1, R2.Pin_0
  GND: U1.GND, IC1.pin10, IC1.pin11, IC1.pin13, IC1.pin15, IC1.pin17, GPS1.pin7, Raspberry_Pi_2.GND, Power.pin3, Power.pin6, C1.1, C2.0, C3.1, C4.0, Q1.S, R3.Pin_0
  N3: U1.XLAT1, XTAL1.pin_1, C1.0
  N4: U1.XLAT2, XTAL1.pin_0, C2.1
  N5: U1.D11_(PWM), IC1.pin14
  N6: U1.D12, IC1.pin8
  N7: U1.D13, IC1.pin16
  N8: IC1.pin1, Raspberry_Pi_2.GPIO8, R1.Pin_0
  N9: IC1.pin2, IC1.pin19, IC1.pin20, GPS1.pin1, Power.pin2, R1.Pin_1
  N10: IC1.pin4, Raspberry_Pi_2.GPIO11
  N11: IC1.pin6, Raspberry_Pi_2.GPIO10
  N12: IC1.pin12, Raspberry_Pi_2.GPIO9
  N13: IC1.pin18, Q1.G, R3.Pin_1
  N14: GPS1.pin5, Raspberry_Pi_2.GPIO15
  N15: GPS1.pin6, Raspberry_Pi_2.GPIO14

notes:
  3.3V
  VBAT
  FIX
  TX
  RX
  GND
  VIN
  PPS
  EN
  BAT2 LVL
  BAT1 LVL
  5V
