# Fritzing sketch navigator (saved by Fritzing 0.9.2b)
breadboards: 1

parts:
  U1 = atmega328 [package=dip]
  XTAL1 = Crystal [frequency="16 Mhz" package=THT]
  IC1 = IC, DIP package, 20 pins [chip_label=74LVC244]
  GPS1 = female pin header, 9 pins [form="♀ (female)"]
  Raspberry_Pi_2 = Raspberry Pi 2
  Power = shrouded pin header, 6 pins [form="♂ (shrouded male)"]

nets:
  N1: U1.XLAT1, XTAL1.pin_1
  N2: U1.XLAT2, XTAL1.pin_0
  N3: IC1.pin10, IC1.pin11, IC1.pin13, IC1.pin15, IC1.pin17, GPS1.pin7, Power.pin3, Power.pin6
  N4: GPS1.pin5, Raspberry_Pi_2.GPIO15
  N5: GPS1.pin6, Raspberry_Pi_2.GPIO14
  GND: Raspberry_Pi_2.GND

notes:
  3.3V
  VBAT
  FIX
  TX
  RX
  GND
  VIN
  PPS
  EN
  BAT2 LVL
  BAT1 LVL
  5V
